// Logisim project Single Cycle Processor.circ as structural Verilog: 7 circuits, main circuit ALU8
// ALU
module ALU8 (
  input  [7:0] X,
  input  [7:0] Y,
  input  [2:0] ALUfunc,
  output [7:0] RESULT,
  output EQ
);

  wire comparator_1_lt;
  wire [7:0] adder_1_out, and_1_out, bit_extender_1_out, or_1_out, shifter_1_out;

  Adder adder_1 (.a(X), .b(Y), .out(adder_1_out));  // open: cin, cout
  Shifter #(.shift("rl")) shifter_1 (.in(X), .\dist (Y[2:0]), .out(shifter_1_out));
  assign and_1_out = X & Y;  // AND_Gate and_1, 8 bits wide
  assign or_1_out = X | Y;  // OR_Gate or_1, 8 bits wide
  Comparator comparator_1 (.a(X), .b(Y), .eq(EQ), .lt(comparator_1_lt));  // open: gt
  assign bit_extender_1_out = {{7{1'b0}}, comparator_1_lt};  // Bit_Extender bit_extender_1
  Multiplexer #(.select(3), .width(8)) multiplexer_1 (
    .in0(adder_1_out), .in1(and_1_out), .in2(or_1_out), .in3(shifter_1_out), .in4(bit_extender_1_out),
    .out(RESULT), .sel(ALUfunc));  // open: in5, in6, in7
endmodule

module RegFile (
  input  WE,
  input  [2:0] Rd,
  input  [7:0] inpt,
  input  [2:0] Rs,
  input  [2:0] Rt,
  input  clk,
  output [7:0] outS,
  output [7:0] outT
);

  wire decoder_1_out0, decoder_1_out1, decoder_1_out2, decoder_1_out3, decoder_1_out4, decoder_1_out5,
       decoder_1_out6, decoder_1_out7;
  wire [7:0] register_1_q, register_2_q, register_3_q, register_4_q, register_5_q, register_6_q,
       register_7_q, register_8_q;

  Decoder #(.select(3)) decoder_1 (
    .out0(decoder_1_out0), .out1(decoder_1_out1), .out2(decoder_1_out2), .out3(decoder_1_out3),
    .out4(decoder_1_out4), .out5(decoder_1_out5), .out6(decoder_1_out6), .out7(decoder_1_out7), .sel(Rd),
    .en(WE));
  Multiplexer #(.select(3), .width(8)) multiplexer_1 (
    .in0(register_1_q), .in1(register_2_q), .in2(register_3_q), .in3(register_4_q), .in4(register_5_q),
    .in5(register_6_q), .in6(register_7_q), .in7(register_8_q), .out(outS), .sel(Rs));
  Multiplexer #(.select(3), .width(8)) multiplexer_2 (
    .in0(register_1_q), .in1(register_2_q), .in2(register_3_q), .in3(register_4_q), .in4(register_5_q),
    .in5(register_6_q), .in6(register_7_q), .in7(register_8_q), .out(outT), .sel(Rt));
  Register #(.trigger("falling")) register_1 (.D(inpt), .en(decoder_1_out0), .clk(clk), .Q(register_1_q));  // open: clr
  Register #(.trigger("falling")) register_2 (.D(inpt), .en(decoder_1_out1), .clk(clk), .Q(register_2_q));  // open: clr
  Register #(.trigger("falling")) register_3 (.D(inpt), .en(decoder_1_out2), .clk(clk), .Q(register_3_q));  // open: clr
  Register #(.trigger("falling")) register_4 (.D(inpt), .en(decoder_1_out3), .clk(clk), .Q(register_4_q));  // open: clr
  Register #(.trigger("falling")) register_5 (.D(inpt), .en(decoder_1_out4), .clk(clk), .Q(register_5_q));  // open: clr
  Register #(.trigger("falling")) register_6 (.D(inpt), .en(decoder_1_out5), .clk(clk), .Q(register_6_q));  // open: clr
  Register #(.trigger("falling")) register_7 (.D(inpt), .en(decoder_1_out6), .clk(clk), .Q(register_7_q));  // open: clr
  Register #(.trigger("falling")) register_8 (.D(inpt), .en(decoder_1_out7), .clk(clk), .Q(register_8_q));  // open: clr
endmodule

module ControlUnit (
  input  [3:0] opcode,
  input  EQ,
  output Branch,
  output [1:0] PCMux,
  output Read,
  output Write,
  output [2:0] ALUfunc,
  output Mux2,
  output WE,
  output [1:0] Mux1,
  output Mux4,
  output [2:0] raAddress
);

  wire and_4_out, and_5_out, and_6_out, and_7_out, and_8_out, and_9_out, and_10_out, and_11_out, and_12_out,
       and_15_out, and_16_out, and_17_out, and_18_out, and_19_out, and_20_out, and_21_out, and_22_out,
       and_23_out, and_24_out, not_1_out, not_2_out, not_3_out, not_4_out, not_5_out;

  not not_1 (not_1_out, opcode[3]);
  not not_2 (not_2_out, opcode[2]);
  not not_3 (not_3_out, opcode[1]);
  not not_4 (not_4_out, opcode[0]);
  not not_5 (not_5_out, EQ);
  and and_1 (ALUfunc[2], opcode[3], opcode[0]);
  and and_2 (ALUfunc[1], opcode[3], not_3_out);
  and and_3 (ALUfunc[0], opcode[2], not_3_out);
  and and_4 (and_4_out, not_2_out, opcode[1]);
  and and_5 (and_5_out, opcode[3], opcode[1], not_4_out);
  and and_6 (and_6_out, not_3_out, opcode[0]);
  and and_7 (and_7_out, opcode[3], opcode[2], opcode[1], not_4_out);
  and and_8 (and_8_out, not_2_out, opcode[0]);
  and and_9 (and_9_out, not_2_out, opcode[1]);
  and and_10 (and_10_out, not_1_out, not_2_out, opcode[0]);
  and and_11 (and_11_out, not_3_out, not_4_out);
  and and_12 (and_12_out, opcode[3], opcode[2]);
  and and_13 (Write, opcode[1], not_4_out);
  and and_14 (Read, not_2_out, not_3_out, opcode[0]);
  and and_15 (and_15_out, opcode[3], not_2_out, opcode[0]);
  and and_16 (and_16_out, opcode[3], not_3_out, opcode[0]);
  and and_17 (and_17_out, opcode[3], opcode[2], opcode[1], not_4_out);
  and and_18 (and_18_out, opcode[2], not_3_out, opcode[0]);
  and and_19 (and_19_out, not_1_out, opcode[2], opcode[0]);
  and and_20 (and_20_out, opcode[3], not_2_out, opcode[0]);
  and and_21 (and_21_out, opcode[3], not_3_out, opcode[0]);
  and and_22 (and_22_out, opcode[2], not_3_out, opcode[0], EQ);
  and and_23 (and_23_out, opcode[3], opcode[2], opcode[1], not_4_out);
  and and_24 (and_24_out, not_1_out, opcode[2], opcode[1], not_5_out);
  or or_1 (Mux1[1], and_4_out, and_5_out);
  or or_2 (Mux1[0], and_6_out, and_7_out);
  or or_3 (Mux2, and_8_out, and_9_out);
  or or_4 (WE, and_10_out, and_11_out, and_12_out);
  or or_5 (PCMux[1], and_15_out, and_16_out, and_17_out);
  or or_6 (PCMux[0], and_18_out, and_19_out);
  or or_7 (Branch, and_20_out, and_21_out, and_22_out, and_23_out, and_24_out);
  and and_25 (Mux4, opcode[3], opcode[2], opcode[1], not_4_out);

  assign raAddress = 3'b111;
endmodule

module CPU (
);

  wire clock_1_out, controlunit_1_branch, controlunit_1_mux2, controlunit_1_mux4, controlunit_1_read,
       controlunit_1_we, controlunit_1_write, eq;
  wire [1:0] and_1_out, bit_extender_1_out, controlunit_1_mux1, controlunit_1_pcmux;
  wire [2:0] controlunit_1_alufunc, controlunit_1_raaddress, instruction_memory_1_rd,
       instruction_memory_1_rs, instruction_memory_1_rt, multiplexer_2_out;
  wire [3:0] instruction_memory_1_op;
  wire [7:0] alu8_1_result, bit_extender_4_out, data_memory_1_data_out, instruction_memory_1_branch_imm,
       instruction_memory_1_immorfunc, multiplexer_3_out, multiplexer_4_out, regfile_1_outs, regfile_1_outt;
  wire [9:0] a, adder_1_out, bit_extender_2_out, bit_extender_3_out, instruction_memory_1_jmp_imm,
       multiplexer_1_out, program_counter_1_pc;

  assign and_1_out = controlunit_1_pcmux & bit_extender_1_out;  // AND_Gate and_1, 2 bits wide
  Clock clock_1 (.out(clock_1_out));
  Multiplexer #(.select(2), .width(10)) multiplexer_1 (
    .in0(adder_1_out), .in1(a), .in2(instruction_memory_1_jmp_imm), .in3(bit_extender_3_out),
    .out(multiplexer_1_out), .sel(and_1_out));
  assign bit_extender_1_out = {{1{controlunit_1_branch}}, controlunit_1_branch};  // Bit_Extender bit_extender_1
  Program_Counter program_counter_1 (.PCinpt(multiplexer_1_out), .clk(clock_1_out), .PC(program_counter_1_pc));
  Adder #(.width(10)) adder_1 (.a(program_counter_1_pc), .b(10'h1), .out(adder_1_out));  // open: cin, cout
  Adder #(.width(10)) adder_2 (.a(program_counter_1_pc), .b(bit_extender_2_out), .out(a));  // open: cin, cout
  assign bit_extender_2_out = {{2{1'b0}}, instruction_memory_1_branch_imm};  // Bit_Extender bit_extender_2
  Instruction_Memory instruction_memory_1 (
    .address(program_counter_1_pc), .op(instruction_memory_1_op), .Rd(instruction_memory_1_rd),
    .ImmOrFunc(instruction_memory_1_immorfunc), .Rs(instruction_memory_1_rs), .Rt(instruction_memory_1_rt),
    .JMP_IMM(instruction_memory_1_jmp_imm), .Branch_Imm(instruction_memory_1_branch_imm));
  assign bit_extender_3_out = {{2{1'b0}}, regfile_1_outs};  // Bit_Extender bit_extender_3
  ControlUnit controlunit_1 (
    .opcode(instruction_memory_1_op), .EQ(eq), .Branch(controlunit_1_branch), .PCMux(controlunit_1_pcmux),
    .Read(controlunit_1_read), .Write(controlunit_1_write), .ALUfunc(controlunit_1_alufunc),
    .Mux2(controlunit_1_mux2), .WE(controlunit_1_we), .Mux1(controlunit_1_mux1), .Mux4(controlunit_1_mux4),
    .raAddress(controlunit_1_raaddress));
  Multiplexer #(.width(3)) multiplexer_2 (
    .in0(instruction_memory_1_rd), .in1(controlunit_1_raaddress), .out(multiplexer_2_out),
    .sel(controlunit_1_mux4));
  Bit_Extender #(.in_width(10), .out_width(8), .\type ("zero")) bit_extender_4 (
    .in(adder_1_out), .out(bit_extender_4_out));
  Multiplexer #(.select(2), .width(8)) multiplexer_3 (
    .in0(alu8_1_result), .in1(data_memory_1_data_out), .in2(instruction_memory_1_immorfunc),
    .in3(bit_extender_4_out), .out(multiplexer_3_out), .sel(controlunit_1_mux1));
  RegFile regfile_1 (
    .WE(controlunit_1_we), .Rd(multiplexer_2_out), .inpt(multiplexer_3_out), .Rs(instruction_memory_1_rs),
    .Rt(instruction_memory_1_rt), .clk(clock_1_out), .outS(regfile_1_outs), .outT(regfile_1_outt));
  Multiplexer #(.width(8)) multiplexer_4 (
    .in0(regfile_1_outt), .in1(instruction_memory_1_immorfunc), .out(multiplexer_4_out),
    .sel(controlunit_1_mux2));
  ALU8 alu8_1 (
    .X(regfile_1_outs), .Y(multiplexer_4_out), .ALUfunc(controlunit_1_alufunc), .RESULT(alu8_1_result),
    .EQ(eq));
  Data_Memory data_memory_1 (
    .addr(alu8_1_result), .Write(controlunit_1_write), .Read(controlunit_1_read), .data_in(regfile_1_outt),
    .clk(clock_1_out), .data_out(data_memory_1_data_out));
endmodule

module Instruction_Memory (
  input  [9:0] address,
  output [3:0] op,
  output [2:0] Rd,
  output [7:0] ImmOrFunc,
  output [2:0] Rs,
  output [2:0] Rt,
  output [9:0] JMP_IMM,
  output [7:0] Branch_Imm
);

  // ROM #(.addrWidth(10), .dataWidth(21), .line("quad"), .misaligned("true")) ProgramROM: pin names not known; wires that end beside it: address, {op, Rs, Rt, Rd[2], JMP_IMM[9:8], Branch_Imm}

  assign ImmOrFunc = Branch_Imm;
  assign JMP_IMM[7:0] = Branch_Imm;
  assign Rd[1:0] = JMP_IMM[9:8];

  // Notes on the sheet:
  //   contents of ProgramROM (hex, n*v repeats v):
  //   0 60307 60502 1c0009 1ee100 60403 e600 20201 eb006 18ec00 42001 1bc000 8d600 bf002 16000c 43004
endmodule

module Data_Memory (
  input  [7:0] addr,
  input  Write,
  input  Read,
  input  [7:0] data_in,
  input  clk,
  output [7:0] data_out
);

  RAM #(.asyncread("true"), .trigger("falling")) ram_1 (
    .addr(addr), .we(Write), .oe(Read), .clk(clk), .din(data_in), .dout(data_out));
endmodule

module Program_Counter (
  input  [9:0] PCinpt,
  input  clk,
  output [9:0] PC
);

  Register #(.trigger("falling"), .width(10)) register_1 (.D(PCinpt), .en(1'b1), .clk(clk), .Q(PC));  // open: clr
endmodule
